// Logisim project control.circ as structural Verilog: 1 circuit, main circuit control
module control (
  input  [31:0] MULT_MEM_32_63,
  input  [31:0] MULT_MEM_0_31,
  input  CLOCK,
  input  RESET,
  output [31:0] MULT_MEM_O_32_63,
  output Mul_Q,
  output [31:0] MULT_MEM_O_0_31,
  output Process,
  output Write_Sig,
  output Process_End
);

  wire and_3_out, Multi_Process_q, not_1_out;

  and and_1 (Write_Sig, CLOCK, Multi_Process_q, not_1_out);
  and and_2 (Process, Multi_Process_q, not_1_out);
  D_Flip_Flop Multi_Process (.clk(CLOCK), .D(1'b1), .Q(Multi_Process_q), .reset(RESET));  // open: Qn, preset, en
  not not_1 (not_1_out, Process_End);
  Counter #(.width(6), .max('h21), .ongoal("stay"), .trigger("falling")) counter_1 (
    .carry(Process_End), .clk(and_3_out), .clr(RESET));  // open: load, D, count, Q
  and and_3 (and_3_out, Multi_Process_q, CLOCK);

  assign Mul_Q = MULT_MEM_0_31[0];
  assign MULT_MEM_O_0_31 = MULT_MEM_0_31;
  assign MULT_MEM_O_32_63 = MULT_MEM_32_63;
endmodule
