// Logisim project datapath.circ as structural Verilog: 2 circuits, main circuit datapath
module datapath (
  input  [31:0] Multiplicant,
  input  [31:0] Multiplier,
  input  CTRL_SIG,
  input  Mul_Q,
  input  PROCESS,
  input  PROCESS_END,
  input  RESET,
  input  [31:0] _1_CTRL_PASS_IN,
  input  [31:0] _2_CTRL_PASS_IN,
  output [31:0] _1_CTRL_PASS_OUT,
  output [31:0] _2_CTRL_PASS_OUT
);

  wire or_1_out;
  wire [31:0] adder_1_out, multiplexer_1_out, multiplexer_2_out, n64_bit_shifter_1_output_bits_0_31,
       n64_bit_shifter_1_output_bits_32_63;

  Multiplexer #(.width(32), .enable("false")) multiplexer_1 (
    .in0({32{1'b0}}), .in1(Multiplicant), .out(multiplexer_1_out), .sel(Mul_Q));
  Adder #(.width(32)) adder_1 (
    .a(n64_bit_shifter_1_output_bits_32_63), .b(multiplexer_1_out), .out(adder_1_out));  // open: cin, cout
  Multiplexer #(.width(32), .enable("false")) multiplexer_2 (
    .in0(Multiplier), .in1(n64_bit_shifter_1_output_bits_0_31), .out(multiplexer_2_out), .sel(PROCESS));
  Register #(.width(32)) register_1 (.D(adder_1_out), .Q(_1_CTRL_PASS_OUT), .clk(or_1_out), .clr(RESET));  // open: en
  Register #(.width(32)) register_2 (
    .D(multiplexer_2_out), .Q(_2_CTRL_PASS_OUT), .clk(or_1_out), .clr(RESET));  // open: en
  or or_1 (or_1_out, PROCESS_END, CTRL_SIG);
  _64_BIT_SHIFTER u_64_bit_shifter_1 (
    .OUTPUT_BITS_32_63(n64_bit_shifter_1_output_bits_32_63),
    .OUTPUT_BITS_0_31(n64_bit_shifter_1_output_bits_0_31), .INPUT_BITS_32_63(_1_CTRL_PASS_IN),
    .INPUT_BITS_0_31(_2_CTRL_PASS_IN));
endmodule

module _64_BIT_SHIFTER (
  input  [31:0] INPUT_BITS_32_63,
  input  [31:0] INPUT_BITS_0_31,
  output [31:0] OUTPUT_BITS_32_63,
  output [31:0] OUTPUT_BITS_0_31
);

  wire [31:31] shifter_2_out;

  Shifter #(.width(32), .shift("lr")) shifter_1 (.in(INPUT_BITS_32_63), .\dist (5'b00001), .out(OUTPUT_BITS_32_63));
  Shifter #(.width(32), .shift("lr")) shifter_2 (
    .in(INPUT_BITS_0_31), .\dist (5'b00001), .out({shifter_2_out[31], OUTPUT_BITS_0_31[30:0]}));

  assign OUTPUT_BITS_0_31[31] = INPUT_BITS_32_63[0];
endmodule
