// Logisim project mult32 (deprecated).circ as structural Verilog: 8 circuits, main circuit datapath
module datapath (
  input  [31:0] Multiplicant,
  input  [31:0] Multiplier,
  input  ENABLE
);

  wire and_1_out, CLOCK_out, control_1_mul_q, control_1_process, control_1_process_end, control_1_write_sig,
       or_1_out, or_2_out, RESET_out;
  wire [31:0] adder_1_out, control_1_mult_mem_o_0_31, control_1_mult_mem_o_32_63, multiplexer_1_out,
       multiplexer_2_out, n64_bit_shifter_1_output_bits_0_31, n64_bit_shifter_1_output_bits_32_63,
       register_1_q, register_2_q;

  // Probe on Multiplicant
  // Probe on Multiplier
  Multiplexer #(.width(32), .enable("false")) multiplexer_1 (
    .in0({32{1'b0}}), .in1(Multiplicant), .out(multiplexer_1_out), .sel(control_1_mul_q));
  // Probe on control_1_mult_mem_o_32_63
  Adder #(.width(32)) adder_1 (
    .a(n64_bit_shifter_1_output_bits_32_63), .b(multiplexer_1_out), .out(adder_1_out));  // open: cin, cout
  Multiplexer #(.width(32), .enable("false")) multiplexer_2 (
    .in0(Multiplier), .in1(n64_bit_shifter_1_output_bits_0_31), .out(multiplexer_2_out),
    .sel(control_1_process));
  Register #(.width(32)) register_1 (.D(adder_1_out), .Q(register_1_q), .clk(or_2_out), .clr(or_1_out));  // open: en
  Register #(.width(32)) register_2 (
    .D(multiplexer_2_out), .Q(register_2_q), .clk(or_2_out), .clr(or_1_out));  // open: en
  or or_1 (or_1_out, RESET_out, ~ENABLE);  // OR_Gate
  Button RESET (.out(RESET_out));
  // Probe on control_1_mult_mem_o_0_31
  or or_2 (or_2_out, control_1_process_end, control_1_write_sig);
  Clock CLOCK (.out(CLOCK_out));
  control control_1 (
    .MULT_MEM_32_63(register_1_q), .MULT_MEM_0_31(register_2_q),
    .MULT_MEM_O_32_63(control_1_mult_mem_o_32_63), .MULT_MEM_O_0_31(control_1_mult_mem_o_0_31),
    .Write_Sig(control_1_write_sig), .Process(control_1_process), .Mul_Q(control_1_mul_q),
    .Process_End(control_1_process_end), .CLOCK(and_1_out), .RESET(or_1_out));
  and and_1 (and_1_out, CLOCK_out, ENABLE);
  _64_bit_shifter u_64_bit_shifter_1 (
    .OUTPUT_BITS_32_63(n64_bit_shifter_1_output_bits_32_63),
    .OUTPUT_BITS_0_31(n64_bit_shifter_1_output_bits_0_31), .INPUT_BITS_32_63(control_1_mult_mem_o_32_63),
    .INPUT_BITS_0_31(control_1_mult_mem_o_0_31));

  // Notes on the sheet:
  //   X
  //   32
  //   2
  //   X
  //   =
  //   +
endmodule

module deprecated__32_bit_shifter (
  input  ENABLE,
  input  [31:0] IN,
  output [31:0] OUT
);

  Multiplexer #(.enable("false")) multiplexer_1 (.in0(IN[1]), .in1(IN[2]), .out(OUT[1]), .sel(ENABLE));
  Multiplexer #(.disabled(0), .enable("false")) multiplexer_2 (.in0(IN[0]), .in1(IN[1]), .out(OUT[0]), .sel(ENABLE));
  Multiplexer #(.enable("false")) multiplexer_3 (.in0(IN[17]), .in1(IN[18]), .out(OUT[17]), .sel(ENABLE));
  Multiplexer #(.disabled(0), .enable("false")) multiplexer_4 (.in0(IN[16]), .in1(IN[17]), .out(OUT[16]), .sel(ENABLE));
  Multiplexer #(.enable("false")) multiplexer_5 (.in0(IN[3]), .in1(IN[4]), .out(OUT[3]), .sel(ENABLE));
  Multiplexer #(.enable("false")) multiplexer_6 (.in0(IN[2]), .in1(IN[3]), .out(OUT[2]), .sel(ENABLE));
  Multiplexer #(.enable("false")) multiplexer_7 (.in0(IN[18]), .in1(IN[19]), .out(OUT[18]), .sel(ENABLE));
  Multiplexer #(.enable("false")) multiplexer_8 (.in0(IN[19]), .in1(IN[20]), .out(OUT[19]), .sel(ENABLE));
  Multiplexer #(.enable("false")) multiplexer_9 (.in0(IN[4]), .in1(IN[5]), .out(OUT[4]), .sel(ENABLE));
  Multiplexer #(.enable("false")) multiplexer_10 (.in0(IN[20]), .in1(IN[21]), .out(OUT[20]), .sel(ENABLE));
  Multiplexer #(.enable("false")) multiplexer_11 (.in0(IN[5]), .in1(IN[6]), .out(OUT[5]), .sel(ENABLE));
  Multiplexer #(.disabled(0), .enable("false")) multiplexer_12 (.in0(IN[6]), .in1(IN[7]), .out(OUT[6]), .sel(ENABLE));
  Multiplexer #(.disabled(0), .enable("false")) multiplexer_13 (
    .in0(IN[22]), .in1(IN[23]), .out(OUT[22]), .sel(ENABLE));
  Multiplexer #(.enable("false")) multiplexer_14 (.in0(IN[21]), .in1(IN[22]), .out(OUT[21]), .sel(ENABLE));
  Multiplexer #(.enable("false")) multiplexer_15 (.in0(IN[7]), .in1(IN[8]), .out(OUT[7]), .sel(ENABLE));
  Multiplexer #(.enable("false")) multiplexer_16 (.in0(IN[23]), .in1(IN[24]), .out(OUT[23]), .sel(ENABLE));
  Multiplexer #(.enable("false")) multiplexer_17 (.in0(IN[8]), .in1(IN[9]), .out(OUT[8]), .sel(ENABLE));
  Multiplexer #(.enable("false")) multiplexer_18 (.in0(IN[9]), .in1(IN[10]), .out(OUT[9]), .sel(ENABLE));
  Multiplexer #(.enable("false")) multiplexer_19 (.in0(IN[25]), .in1(IN[26]), .out(OUT[25]), .sel(ENABLE));
  Multiplexer #(.enable("false")) multiplexer_20 (.in0(IN[24]), .in1(IN[25]), .out(OUT[24]), .sel(ENABLE));
  Multiplexer #(.enable("false")) multiplexer_21 (.in0(IN[10]), .in1(IN[11]), .out(OUT[10]), .sel(ENABLE));
  Multiplexer #(.enable("false")) multiplexer_22 (.in0(IN[11]), .in1(IN[12]), .out(OUT[11]), .sel(ENABLE));
  Multiplexer #(.enable("false")) multiplexer_23 (.in0(IN[27]), .in1(IN[28]), .out(OUT[27]), .sel(ENABLE));
  Multiplexer #(.enable("false")) multiplexer_24 (.in0(IN[26]), .in1(IN[27]), .out(OUT[26]), .sel(ENABLE));
  Multiplexer #(.enable("false")) multiplexer_25 (.in0(IN[12]), .in1(IN[13]), .out(OUT[12]), .sel(ENABLE));
  Multiplexer #(.enable("false")) multiplexer_26 (.in0(IN[28]), .in1(IN[29]), .out(OUT[28]), .sel(ENABLE));
  Multiplexer #(.enable("false")) multiplexer_27 (.in0(IN[13]), .in1(IN[14]), .out(OUT[13]), .sel(ENABLE));
  Multiplexer #(.enable("false")) multiplexer_28 (.in0(IN[14]), .in1(IN[15]), .out(OUT[14]), .sel(ENABLE));
  Multiplexer #(.enable("false")) multiplexer_29 (.in0(IN[30]), .in1(IN[31]), .out(OUT[30]), .sel(ENABLE));
  Multiplexer #(.enable("false")) multiplexer_30 (.in0(IN[29]), .in1(IN[30]), .out(OUT[29]), .sel(ENABLE));
  Multiplexer #(.enable("false")) multiplexer_31 (.in0(IN[15]), .in1(IN[16]), .out(OUT[15]), .sel(ENABLE));
  Multiplexer #(.enable("false")) multiplexer_32 (.in0(IN[31]), .in1(1'b0), .out(OUT[31]), .sel(ENABLE));
endmodule

module deprecated__64_bit_shifter (
  input  ENABLE,
  input  [31:0] INPUT_BITS_32_63,
  input  [31:0] INPUT_BITS_0_31,
  output [31:0] OUTPUT_BITS_32_63,
  output [31:0] OUTPUT_BITS_0_31
);

  wire [31:31] deprecated_32_bit_shifter_2_out;

  deprecated__32_bit_shifter deprecated_32_bit_shifter_1 (
    .ENABLE(ENABLE), .OUT(OUTPUT_BITS_32_63), .IN(INPUT_BITS_32_63));
  Multiplexer #(.disabled(0), .enable("false")) multiplexer_1 (
    .in0(deprecated_32_bit_shifter_2_out[31]), .in1(INPUT_BITS_32_63[0]), .out(OUTPUT_BITS_0_31[31]),
    .sel(ENABLE));
  deprecated__32_bit_shifter deprecated_32_bit_shifter_2 (
    .ENABLE(ENABLE), .OUT({deprecated_32_bit_shifter_2_out[31], OUTPUT_BITS_0_31[30:0]}), .IN(INPUT_BITS_0_31));
endmodule

module control (
  input  [31:0] MULT_MEM_32_63,
  input  [31:0] MULT_MEM_0_31,
  input  CLOCK,
  input  RESET,
  output [31:0] MULT_MEM_O_32_63,
  output Mul_Q,
  output [31:0] MULT_MEM_O_0_31,
  output Process,
  output Write_Sig,
  output Process_End
);

  wire and_3_out, Multi_Process_q, not_1_out;

  and and_1 (Write_Sig, CLOCK, Multi_Process_q, not_1_out);
  and and_2 (Process, Multi_Process_q, not_1_out);
  D_Flip_Flop Multi_Process (.clk(CLOCK), .D(1'b1), .Q(Multi_Process_q), .reset(RESET));  // open: Qn, preset, en
  not not_1 (not_1_out, Process_End);
  Counter #(.width(6), .max('h21), .ongoal("stay"), .trigger("falling")) counter_1 (
    .carry(Process_End), .clk(and_3_out), .clr(RESET));  // open: load, D, count, Q
  and and_3 (and_3_out, Multi_Process_q, CLOCK);

  assign Mul_Q = MULT_MEM_0_31[0];
  assign MULT_MEM_O_0_31 = MULT_MEM_0_31;
  assign MULT_MEM_O_32_63 = MULT_MEM_32_63;
endmodule

module deprecated__32_bit_adder (
  input  [31:0] A,
  input  [31:0] B,
  input  C_in,
  output C_out,
  output [31:0] S
);

  wire deprecated_4_bit_adder_1_c_out, deprecated_4_bit_adder_3_c_out, deprecated_4_bit_adder_4_c_out,
       deprecated_4_bit_adder_5_c_out, deprecated_4_bit_adder_6_c_out, deprecated_4_bit_adder_7_c_out,
       deprecated_4_bit_adder_8_c_out;

  deprecated__4__bit_adder deprecated_4_bit_adder_1 (
    .C_Out(deprecated_4_bit_adder_1_c_out), .C_In(deprecated_4_bit_adder_3_c_out), .A(A[27:24]),
    .B(B[27:24]), .S(S[27:24]));
  deprecated__4__bit_adder deprecated_4_bit_adder_2 (
    .C_Out(C_out), .C_In(deprecated_4_bit_adder_1_c_out), .A(A[31:28]), .B(B[31:28]), .S(S[31:28]));
  deprecated__4__bit_adder deprecated_4_bit_adder_3 (
    .C_Out(deprecated_4_bit_adder_3_c_out), .C_In(deprecated_4_bit_adder_4_c_out), .A(A[23:20]),
    .B(B[23:20]), .S(S[23:20]));
  deprecated__4__bit_adder deprecated_4_bit_adder_4 (
    .C_Out(deprecated_4_bit_adder_4_c_out), .C_In(deprecated_4_bit_adder_5_c_out), .A(A[19:16]),
    .B(B[19:16]), .S(S[19:16]));
  deprecated__4__bit_adder deprecated_4_bit_adder_5 (
    .C_Out(deprecated_4_bit_adder_5_c_out), .C_In(deprecated_4_bit_adder_6_c_out), .A(A[15:12]),
    .B(B[15:12]), .S(S[15:12]));
  deprecated__4__bit_adder deprecated_4_bit_adder_6 (
    .C_Out(deprecated_4_bit_adder_6_c_out), .C_In(deprecated_4_bit_adder_8_c_out), .A(A[11:8]), .B(B[11:8]),
    .S(S[11:8]));
  deprecated__4__bit_adder deprecated_4_bit_adder_7 (
    .C_Out(deprecated_4_bit_adder_7_c_out), .C_In(C_in), .A(A[3:0]), .B(B[3:0]), .S(S[3:0]));
  deprecated__4__bit_adder deprecated_4_bit_adder_8 (
    .C_Out(deprecated_4_bit_adder_8_c_out), .C_In(deprecated_4_bit_adder_7_c_out), .A(A[7:4]), .B(B[7:4]),
    .S(S[7:4]));
endmodule

module deprecated__Full_Adder (
  input  A,
  input  B,
  input  C_In,
  output C_out,
  output S
);

  wire and_1_out, and_2_out, xor_2_out;

  and and_1 (and_1_out, xor_2_out, C_In);
  and and_2 (and_2_out, A, B);
  xor xor_1 (C_out, and_2_out, and_1_out);
  xor xor_2 (xor_2_out, A, B);
  xor xor_3 (S, xor_2_out, C_In);
endmodule

module deprecated__4__bit_adder (
  input  [3:0] A,
  input  [3:0] B,
  input  C_In,
  output C_Out,
  output [3:0] S
);

  wire deprecated_full_adder_2_c_out, deprecated_full_adder_3_c_out, deprecated_full_adder_4_c_out;

  deprecated__Full_Adder deprecated_full_adder_1 (
    .C_out(C_Out), .C_In(deprecated_full_adder_2_c_out), .A(A[3]), .B(B[3]), .S(S[3]));
  deprecated__Full_Adder deprecated_full_adder_2 (
    .C_out(deprecated_full_adder_2_c_out), .C_In(deprecated_full_adder_4_c_out), .A(A[2]), .B(B[2]), .S(S[2]));
  deprecated__Full_Adder deprecated_full_adder_3 (
    .C_out(deprecated_full_adder_3_c_out), .C_In(C_In), .A(A[0]), .B(B[0]), .S(S[0]));
  deprecated__Full_Adder deprecated_full_adder_4 (
    .C_out(deprecated_full_adder_4_c_out), .C_In(deprecated_full_adder_3_c_out), .A(A[1]), .B(B[1]), .S(S[1]));
endmodule

module _64_bit_shifter (
  input  [31:0] INPUT_BITS_32_63,
  input  [31:0] INPUT_BITS_0_31,
  output [31:0] OUTPUT_BITS_32_63,
  output [31:0] OUTPUT_BITS_0_31
);

  wire [31:31] shifter_2_out;

  Shifter #(.width(32), .shift("lr")) shifter_1 (.in(INPUT_BITS_32_63), .\dist (5'b00001), .out(OUTPUT_BITS_32_63));
  Shifter #(.width(32), .shift("lr")) shifter_2 (
    .in(INPUT_BITS_0_31), .\dist (5'b00001), .out({shifter_2_out[31], OUTPUT_BITS_0_31[30:0]}));

  assign OUTPUT_BITS_0_31[31] = INPUT_BITS_32_63[0];
endmodule
