// Logisim project mult32.circ as structural Verilog: 1 circuit, main circuit mult32
module mult32 (
  input  [31:0] Multiplicant,
  input  [31:0] Multiplier,
  input  ENABLE
);

  wire and_1_out, CLOCK_out, control_1_mul_q, control_1_process, control_1_process_end, control_1_write_sig,
       or_1_out, RESET_out;
  wire [31:0] control_1_mult_mem_o_0_31, control_1_mult_mem_o_32_63, datapath_1__1_ctrl_pass_out,
       datapath_1__2_ctrl_pass_out;

  // Probe on Multiplicant
  // Probe on Multiplier
  // Probe on control_1_mult_mem_o_32_63
  or or_1 (or_1_out, RESET_out, ~ENABLE);  // OR_Gate
  Button RESET (.out(RESET_out));
  datapath datapath_1 (
    .Multiplicant(Multiplicant), .Multiplier(Multiplier), ._1_CTRL_PASS_IN(control_1_mult_mem_o_32_63),
    ._2_CTRL_PASS_IN(control_1_mult_mem_o_0_31), ._1_CTRL_PASS_OUT(datapath_1__1_ctrl_pass_out),
    ._2_CTRL_PASS_OUT(datapath_1__2_ctrl_pass_out), .RESET(or_1_out), .CTRL_SIG(control_1_write_sig),
    .PROCESS(control_1_process), .Mul_Q(control_1_mul_q), .PROCESS_END(control_1_process_end));
  // Probe on control_1_mult_mem_o_0_31
  and and_1 (and_1_out, CLOCK_out, ENABLE);
  Clock CLOCK (.out(CLOCK_out));
  control control_1 (
    .MULT_MEM_32_63(datapath_1__1_ctrl_pass_out), .MULT_MEM_0_31(datapath_1__2_ctrl_pass_out),
    .MULT_MEM_O_32_63(control_1_mult_mem_o_32_63), .MULT_MEM_O_0_31(control_1_mult_mem_o_0_31),
    .Write_Sig(control_1_write_sig), .Process(control_1_process), .Mul_Q(control_1_mul_q),
    .Process_End(control_1_process_end), .CLOCK(and_1_out), .RESET(or_1_out));

  // Notes on the sheet:
  //   X
  //   32
  //   X
  //   2
  //   =
  //   +
endmodule
