// Logisim project project 1.circ as structural Verilog: 1 circuit, main circuit main
module main (
);

  wire and_1_out, and_2_out, and_3_out, B1_out, B2_out, decoder_1_out0, decoder_1_out1, decoder_1_out2,
       decoder_1_out3, decoder_1_out5, decoder_1_out6, decoder_1_out7, nor_1_out, not_1_out, not_2_out,
       Reset_out, xor_1_out;
  wire [2:0] adder_1_out, multiplexer_1_out, register_1_q, subtractor_1_out;

  LED minus_3 (.in(decoder_1_out5));
  nor nor_1 (nor_1_out, decoder_1_out5, decoder_1_out3);
  and and_1 (and_1_out, not_1_out, B1_out);
  not not_1 (not_1_out, B1_out);
  Button B1 (.out(B1_out));
  LED minus_2 (.in(decoder_1_out6));
  LED minus_1 (.in(decoder_1_out7));
  Decoder #(.select(3), .enable("false")) decoder_1 (
    .out0(decoder_1_out0), .out1(decoder_1_out1), .out2(decoder_1_out2), .out3(decoder_1_out3),
    .out5(decoder_1_out5), .out6(decoder_1_out6), .out7(decoder_1_out7), .sel(register_1_q));  // open: out4
  Multiplexer #(.width(3), .enable("false")) multiplexer_1 (
    .in0(subtractor_1_out), .in1(adder_1_out), .out(multiplexer_1_out), .sel(and_3_out));
  and and_2 (and_2_out, nor_1_out, xor_1_out);
  LED _0 (.in(decoder_1_out0));
  Register #(.width(3), .trigger("falling")) register_1 (
    .D(multiplexer_1_out), .Q(register_1_q), .clk(and_2_out), .clr(Reset_out));  // open: en
  xor xor_1 (xor_1_out, and_1_out, and_3_out);
  LED _1 (.in(decoder_1_out1));
  LED _2 (.in(decoder_1_out2));
  Adder #(.width(3)) adder_1 (.a(register_1_q), .b(3'b001), .out(adder_1_out));  // open: cin, cout
  Subtractor #(.width(3)) subtractor_1 (.a(register_1_q), .b(3'b001), .out(subtractor_1_out));  // open: bin, bout
  not not_2 (not_2_out, B2_out);
  LED _3 (.in(decoder_1_out3));
  Button Reset (.out(Reset_out));
  and and_3 (and_3_out, not_2_out, B2_out);
  Button B2 (.out(B2_out));
endmodule
