// Logisim project project 2.circ as structural Verilog: 1 circuit, main circuit main
module main (
  input  [15:0] in_1,
  input  [15:0] in_2,
  output [15:0] out_3
);

  wire and_1_out, and_2_out, and_3_out, buffer_1_out, buffer_2_out, clock_1_out, comparator_1_lt, d_ff_1_q,
       d_ff_1_qn, not_1_out, or_1_out, Reset_out, Start_out;
  wire [15:0] a_q, adder_1_out, b_q, multiplexer_1_out, subtractor_1_out;

  Button Start (.out(Start_out));
  buf buffer_1 (buffer_1_out, Start_out);
  D_Flip_Flop d_ff_1 (
    .clk(buffer_1_out), .D(Start_out), .Q(d_ff_1_q), .Qn(d_ff_1_qn), .reset(Reset_out));  // open: preset, en
  buf buffer_2 (buffer_2_out, d_ff_1_qn);
  Button Reset (.out(Reset_out));
  LED ENTER_YOUR_NUMBERS_THEN_PRESS_START_TO_CALCULATE (.in(buffer_2_out));
  // Probe on in_1
  and and_1 (and_1_out, buffer_2_out, Start_out);
  // Probe on in_2
  Register #(.width(16)) b (.D(in_1), .Q(b_q), .clk(and_1_out), .clr(Reset_out));  // open: en
  Register #(.width(16)) mult (.D(adder_1_out), .Q(out_3), .clk(and_2_out), .clr(Reset_out));  // open: en
  // Probe on out_3
  Register #(.width(16)) a (.D(multiplexer_1_out), .Q(a_q), .clk(or_1_out), .clr(Reset_out));  // open: en
  Multiplexer #(.width(16), .enable("false")) multiplexer_1 (
    .in0(in_2), .in1(subtractor_1_out), .out(multiplexer_1_out), .sel(d_ff_1_q));
  or or_1 (or_1_out, and_1_out, and_2_out);
  Adder #(.width(16)) adder_1 (.a(b_q), .b(out_3), .out(adder_1_out));  // open: cin, cout
  Subtractor #(.width(16)) subtractor_1 (.a(a_q), .b({16{1'b0}}), .out(subtractor_1_out), .bin(1'b1));  // open: bout
  Comparator #(.width(16)) comparator_1 (.a(subtractor_1_out), .b({16{1'b0}}), .lt(comparator_1_lt));  // open: gt, eq
  Clock clock_1 (.out(clock_1_out));
  not not_1 (not_1_out, comparator_1_lt);
  and and_2 (and_2_out, d_ff_1_q, clock_1_out, not_1_out);
  and and_3 (and_3_out, comparator_1_lt, d_ff_1_q);
  LED CALCULATION_IS_DONE_PRESS_RESET (.in(and_3_out));
endmodule
