// Logisim project proj.circ as structural Verilog: 2 circuits, main circuit main
module main (
);

  wire A_out, and_1_out, and_2_out, and_3_out, and_4_out, and_5_out, and_6_out, and_7_out, and_8_out,
       and_9_out, and_10_out, and_11_out, and_12_out, and_13_out, and_14_out, and_15_out, and_16_out,
       and_17_out, and_18_out, and_19_out, and_20_out, and_21_out, and_22_out, and_23_out, and_24_out,
       and_25_out, and_26_out, and_27_out, and_28_out, and_29_out, and_30_out, and_31_out, and_32_out,
       and_33_out, and_34_out, and_35_out, and_36_out, and_37_out, and_38_out, B_out, buffer_1_out,
       buffer_2_out, buffer_3_out, buffer_4_out, buffer_5_out, buffer_6_out, buffer_7_out, buffer_8_out,
       buffer_9_out, buffer_10_out, buffer_11_out, buffer_12_out, buffer_13_out, buffer_14_out,
       buffer_15_out, buffer_16_out, buffer_17_out, buffer_18_out, buffer_19_out, buffer_20_out,
       buffer_21_out, buffer_22_out, buffer_23_out, buffer_24_out, buffer_25_out, buffer_26_out,
       buffer_27_out, buffer_28_out, C_out, clock_1_out, comparator_1_eq, comparator_2_eq, comparator_3_eq,
       comparator_4_gt, comparator_5_gt, comparator_6_gt, comparator_7_gt, comparator_8_gt, comparator_9_gt,
       comparator_10_gt, comparator_11_gt, comparator_12_gt, comparator_13_gt, comparator_14_eq,
       comparator_15_gt, comparator_16_eq, comparator_17_eq, comparator_18_eq, comparator_19_eq,
       comparator_20_eq, comparator_21_eq, comparator_22_eq, comparator_23_eq, comparator_24_eq,
       comparator_25_eq, comparator_26_eq, comparator_27_eq, comparator_28_eq, comparator_29_eq,
       comparator_30_eq, comparator_31_eq, counter_1_carry, counter_2_carry, counter_4_carry, counter_6_q,
       d_ff_1_qn, d_ff_2_qn, d_ff_3_qn, d_ff_4_qn, d_ff_5_q, d_ff_5_qn, d_ff_6_qn, d_ff_7_qn, d_ff_8_qn,
       d_ff_9_qn, d_ff_10_qn, d_ff_11_qn, d_ff_12_qn, d_ff_13_qn, d_ff_14_q, d_ff_14_qn, d_ff_15_qn,
       d_ff_16_qn, d_ff_17_qn, d_ff_18_qn, d_ff_19_qn, d_ff_20_qn, d_ff_21_qn, d_ff_22_qn, d_ff_23_qn,
       d_ff_24_qn, d_ff_25_qn, d_ff_26_qn, d_ff_27_qn, d_ff_28_qn, D_out, E_out, F_out, G_out, H_out, I_out,
       J_out, K_out, L_out, M_out, N_out, nor_1_out, not_1_out, not_2_out, not_3_out, not_4_out, not_5_out,
       not_6_out, not_7_out, not_8_out, not_9_out, not_10_out, not_11_out, not_12_out, not_13_out,
       not_14_out, not_15_out, not_16_out, O_out, or_1_out, or_2_out, P_out, Q_out, R_out, RESET_out, S_out,
       T_out, U_out, undriven, V_out, W_out, X_out, Y_out, Z_out;
  wire [2:0] counter_4_q;
  wire [3:0] counter_1_q, counter_3_q;
  wire [4:0] priority_encoder_1_out, register_1_q;
  wire [6:0] adder_1_out, counter_5_q, multiplexer_1_out, multiplexer_2_out;

  Counter #(.width(4), .max('h8), .ongoal("stay")) counter_1 (
    .Q(counter_1_q), .carry(counter_1_carry), .clk(and_23_out), .clr(and_18_out));  // open: load, D, count
  and and_1 (and_1_out, and_18_out, nor_1_out);
  buf buffer_1 (buffer_1_out, A_out);
  Button A (.out(A_out));
  Button RESET (.out(RESET_out));
  Multiplexer #(.select(3), .width(7), .enable("false")) multiplexer_1 (
    .in0({7{1'b0}}), .in1({7{1'b0}}), .in2({7{1'b0}}), .in3(7'b1101000), .in4(7'b1100101), .in5(7'b1101100),
    .in6(7'b1101100), .in7(7'b1101111), .out(multiplexer_1_out), .sel(counter_1_q[2:0]));
  D_Flip_Flop d_ff_1 (
    .clk(buffer_1_out), .D(A_out), .Qn(d_ff_1_qn), .en(and_1_out), .reset(RESET_out));  // open: Q, preset
  D_Flip_Flop d_ff_2 (
    .clk(buffer_2_out), .D(B_out), .Qn(d_ff_2_qn), .en(and_1_out), .reset(RESET_out));  // open: Q, preset
  buf buffer_2 (buffer_2_out, B_out);
  buf buffer_3 (buffer_3_out, C_out);
  D_Flip_Flop d_ff_3 (
    .clk(buffer_3_out), .D(C_out), .Qn(d_ff_3_qn), .en(and_1_out), .reset(RESET_out));  // open: Q, preset
  D_Flip_Flop d_ff_4 (
    .clk(buffer_4_out), .D(D_out), .Qn(d_ff_4_qn), .en(and_1_out), .reset(RESET_out));  // open: Q, preset
  buf buffer_4 (buffer_4_out, D_out);
  Button B (.out(B_out));
  Button C (.out(C_out));
  Comparator #(.width(7)) comparator_1 (.a(multiplexer_1_out), .b(adder_1_out), .eq(comparator_1_eq));  // open: gt, lt
  buf buffer_5 (buffer_5_out, comparator_1_eq);
  and and_2 (and_2_out, d_ff_5_qn, and_23_out, counter_1_carry);
  Counter #(.width(3), .max('h5), .ongoal("stay")) counter_2 (
    .count(and_3_out), .carry(counter_2_carry), .clk(and_23_out), .clr(RESET_out));  // open: load, D, Q
  and and_3 (and_3_out, comparator_1_eq, d_ff_5_q);
  buf buffer_6 (buffer_6_out, E_out);
  and and_4 (and_4_out, A_out, d_ff_1_qn);
  and and_5 (and_5_out, B_out, d_ff_2_qn);
  and and_6 (and_6_out, C_out, d_ff_3_qn);
  and and_7 (and_7_out, D_out, d_ff_4_qn);
  Button E (.out(E_out));
  Button D (.out(D_out));
  D_Flip_Flop d_ff_5 (
    .clk(buffer_5_out), .D(comparator_1_eq), .Q(d_ff_5_q), .Qn(d_ff_5_qn), .reset(and_18_out));  // open: preset, en
  Counter #(.width(4), .max('ha), .ongoal("stay")) counter_3 (
    .count(and_2_out), .Q(counter_3_q), .clk(and_2_out), .clr(RESET_out));  // open: load, D, carry
  D_Flip_Flop d_ff_6 (
    .clk(buffer_6_out), .D(E_out), .Qn(d_ff_6_qn), .en(and_1_out), .reset(RESET_out));  // open: Q, preset
  D_Flip_Flop d_ff_7 (
    .clk(buffer_7_out), .D(F_out), .Qn(d_ff_7_qn), .en(and_1_out), .reset(RESET_out));  // open: Q, preset
  buf buffer_7 (buffer_7_out, F_out);
  buf buffer_8 (buffer_8_out, G_out);
  D_Flip_Flop d_ff_8 (
    .clk(buffer_8_out), .D(G_out), .Qn(d_ff_8_qn), .en(and_1_out), .reset(RESET_out));  // open: Q, preset
  buf buffer_9 (buffer_9_out, H_out);
  D_Flip_Flop d_ff_9 (
    .clk(buffer_9_out), .D(H_out), .Qn(d_ff_9_qn), .en(and_1_out), .reset(RESET_out));  // open: Q, preset
  Button G (.out(G_out));
  Button F (.out(F_out));
  Multiplexer #(.select(3), .width(7), .enable("false")) multiplexer_2 (
    .in0({7{1'b0}}), .in1({7{1'b0}}), .in2({7{1'b0}}), .in3(7'b1101000), .in4(7'b1100101), .in5(7'b1101100),
    .in6(7'b1101100), .in7(7'b1101111), .out(multiplexer_2_out), .sel(counter_4_q));
  Counter #(.width(3), .max('h7), .ongoal("stay")) counter_4 (
    .Q(counter_4_q), .carry(counter_4_carry), .clk(clock_1_out), .clr(RESET_out));  // open: load, D, count
  Comparator #(.width(4)) comparator_2 (.a(counter_3_q), .b(4'b1010), .eq(comparator_2_eq));  // open: gt, lt
  and and_8 (and_8_out, and_18_out, undriven);
  Priority_Encoder #(.select(5), .disabled(0)) priority_encoder_1 (
    .in0(and_4_out), .in1(and_5_out), .in2(and_6_out), .in3(and_7_out), .in4(and_9_out), .in5(and_10_out),
    .in6(and_11_out), .in7(and_12_out), .in8(and_13_out), .in9(and_14_out), .in10(and_15_out),
    .in11(and_16_out), .in12(and_19_out), .in13(and_20_out), .in14(and_21_out), .in15(and_22_out),
    .in16(and_24_out), .in17(and_25_out), .in18(and_26_out), .in19(and_27_out), .in20(and_28_out),
    .in21(and_29_out), .in22(and_30_out), .in23(and_31_out), .in24(and_32_out), .in25(and_33_out),
    .out(priority_encoder_1_out));  // open: in26, in27, in28, in29, in30, in31
  and and_9 (and_9_out, E_out, d_ff_6_qn);
  buf buffer_10 (buffer_10_out, I_out);
  and and_10 (and_10_out, F_out, d_ff_7_qn);
  and and_11 (and_11_out, G_out, d_ff_8_qn);
  and and_12 (and_12_out, H_out, d_ff_9_qn);
  Button H (.out(H_out));
  Button I (.out(I_out));
  Register #(.width(5)) register_1 (
    .D(priority_encoder_1_out), .Q(register_1_q), .clk(and_8_out), .clr(RESET_out));  // open: en
  D_Flip_Flop d_ff_10 (
    .clk(buffer_10_out), .D(I_out), .Qn(d_ff_10_qn), .en(and_1_out), .reset(RESET_out));  // open: Q, preset
  D_Flip_Flop d_ff_11 (
    .clk(buffer_11_out), .D(J_out), .Qn(d_ff_11_qn), .en(and_1_out), .reset(RESET_out));  // open: Q, preset
  buf buffer_11 (buffer_11_out, J_out);
  D_Flip_Flop d_ff_12 (
    .clk(buffer_12_out), .D(K_out), .Qn(d_ff_12_qn), .en(and_1_out), .reset(RESET_out));  // open: Q, preset
  buf buffer_12 (buffer_12_out, K_out);
  buf buffer_13 (buffer_13_out, L_out);
  D_Flip_Flop d_ff_13 (
    .clk(buffer_13_out), .D(L_out), .Qn(d_ff_13_qn), .en(and_1_out), .reset(RESET_out));  // open: Q, preset
  Button K (.out(K_out));
  Button J (.out(J_out));
  not not_1 (not_1_out, comparator_3_eq);
  not not_2 (not_2_out, counter_4_carry);
  Comparator #(.width(7)) comparator_3 (.a(multiplexer_2_out), .b({7{1'b0}}), .eq(comparator_3_eq));  // open: gt, lt
  TTY tty_1 (.data(multiplexer_1_out), .clk(d_ff_5_q), .clr(RESET_out));  // open: we
  Adder #(.width(7)) adder_1 (.a(7'b1100001), .b({2'b00, register_1_q}), .out(adder_1_out));  // open: cin, cout
  and and_13 (and_13_out, I_out, d_ff_10_qn);
  buf buffer_14 (buffer_14_out, M_out);
  and and_14 (and_14_out, J_out, d_ff_11_qn);
  and and_15 (and_15_out, K_out, d_ff_12_qn);
  and and_16 (and_16_out, L_out, d_ff_13_qn);
  Button M (.out(M_out));
  Button L (.out(L_out));
  and and_17 (and_17_out, not_1_out, not_2_out, clock_1_out);
  D_Flip_Flop d_ff_14 (
    .clk(and_8_out), .D(1'b1), .Q(d_ff_14_q), .Qn(d_ff_14_qn), .reset(or_1_out));  // open: preset, en
  or or_1 (or_1_out, RESET_out, and_2_out, counter_1_carry);
  D_Flip_Flop d_ff_15 (
    .clk(buffer_14_out), .D(M_out), .Qn(d_ff_15_qn), .en(and_1_out), .reset(RESET_out));  // open: Q, preset
  buf buffer_15 (buffer_15_out, N_out);
  D_Flip_Flop d_ff_16 (
    .clk(buffer_15_out), .D(N_out), .Qn(d_ff_16_qn), .en(and_1_out), .reset(RESET_out));  // open: Q, preset
  D_Flip_Flop d_ff_17 (
    .clk(buffer_16_out), .D(O_out), .Qn(d_ff_17_qn), .en(and_1_out), .reset(RESET_out));  // open: Q, preset
  buf buffer_16 (buffer_16_out, O_out);
  D_Flip_Flop d_ff_18 (
    .clk(buffer_17_out), .D(P_out), .Qn(d_ff_18_qn), .en(and_1_out), .reset(RESET_out));  // open: Q, preset
  buf buffer_17 (buffer_17_out, P_out);
  Button N (.out(N_out));
  Button O (.out(O_out));
  Counter #(.width(7), .max('h7f), .ongoal("stay")) counter_5 (
    .Q(counter_5_q), .clk(and_17_out), .clr(RESET_out));  // open: load, D, count, carry
  and and_18 (and_18_out, d_ff_14_qn, nor_1_out);
  and and_19 (and_19_out, M_out, d_ff_15_qn);
  buf buffer_18 (buffer_18_out, Q_out);
  and and_20 (and_20_out, N_out, d_ff_16_qn);
  and and_21 (and_21_out, O_out, d_ff_17_qn);
  and and_22 (and_22_out, P_out, d_ff_18_qn);
  Button P (.out(P_out));
  Button Q (.out(Q_out));
  and and_23 (and_23_out, d_ff_14_q, clock_1_out, counter_6_q);
  D_Flip_Flop d_ff_19 (
    .clk(buffer_18_out), .D(Q_out), .Qn(d_ff_19_qn), .en(and_1_out), .reset(RESET_out));  // open: Q, preset
  D_Flip_Flop d_ff_20 (
    .clk(buffer_19_out), .D(R_out), .Qn(d_ff_20_qn), .en(and_1_out), .reset(RESET_out));  // open: Q, preset
  buf buffer_19 (buffer_19_out, R_out);
  buf buffer_20 (buffer_20_out, S_out);
  D_Flip_Flop d_ff_21 (
    .clk(buffer_20_out), .D(S_out), .Qn(d_ff_21_qn), .en(and_1_out), .reset(RESET_out));  // open: Q, preset
  buf buffer_21 (buffer_21_out, T_out);
  D_Flip_Flop d_ff_22 (
    .clk(buffer_21_out), .D(T_out), .Qn(d_ff_22_qn), .en(and_1_out), .reset(RESET_out));  // open: Q, preset
  Button S (.out(S_out));
  Button R (.out(R_out));
  LED YOU_GUESSED (.in(counter_2_carry));
  Counter #(.width(1), .max('h1), .ongoal("stay")) counter_6 (
    .D(clock_1_out), .Q(counter_6_q), .clk(buffer_22_out), .clr(and_18_out));  // open: load, count, carry
  buf buffer_22 (buffer_22_out, clock_1_out);
  buf buffer_23 (buffer_23_out, U_out);
  and and_24 (and_24_out, Q_out, d_ff_19_qn);
  and and_25 (and_25_out, R_out, d_ff_20_qn);
  and and_26 (and_26_out, S_out, d_ff_21_qn);
  and and_27 (and_27_out, T_out, d_ff_22_qn);
  Button U (.out(U_out));
  Button T (.out(T_out));
  not not_3 (not_3_out, counter_4_carry);
  nor nor_1 (nor_1_out, counter_2_carry, not_3_out, comparator_2_eq);
  Clock clock_1 (.out(clock_1_out));
  D_Flip_Flop d_ff_23 (
    .clk(buffer_23_out), .D(U_out), .Qn(d_ff_23_qn), .en(and_1_out), .reset(RESET_out));  // open: Q, preset
  D_Flip_Flop d_ff_24 (
    .clk(buffer_24_out), .D(V_out), .Qn(d_ff_24_qn), .en(and_1_out), .reset(RESET_out));  // open: Q, preset
  buf buffer_24 (buffer_24_out, V_out);
  D_Flip_Flop d_ff_25 (
    .clk(buffer_25_out), .D(W_out), .Qn(d_ff_25_qn), .en(and_1_out), .reset(RESET_out));  // open: Q, preset
  buf buffer_25 (buffer_25_out, W_out);
  D_Flip_Flop d_ff_26 (
    .clk(buffer_26_out), .D(X_out), .Qn(d_ff_26_qn), .en(and_1_out), .reset(RESET_out));  // open: Q, preset
  buf buffer_26 (buffer_26_out, X_out);
  Button V (.out(V_out));
  Button W (.out(W_out));
  buf buffer_27 (buffer_27_out, Y_out);
  and and_28 (and_28_out, U_out, d_ff_23_qn);
  and and_29 (and_29_out, V_out, d_ff_24_qn);
  and and_30 (and_30_out, W_out, d_ff_25_qn);
  and and_31 (and_31_out, X_out, d_ff_26_qn);
  Button Y (.out(Y_out));
  Button X (.out(X_out));
  D_Flip_Flop d_ff_27 (
    .clk(buffer_27_out), .D(Y_out), .Qn(d_ff_27_qn), .en(and_1_out), .reset(RESET_out));  // open: Q, preset
  D_Flip_Flop d_ff_28 (
    .clk(buffer_28_out), .D(Z_out), .Qn(d_ff_28_qn), .en(and_1_out), .reset(RESET_out));  // open: Q, preset
  buf buffer_28 (buffer_28_out, Z_out);
  Button Z (.out(Z_out));
  LED GAME_OVER (.in(comparator_2_eq));
  and and_32 (and_32_out, Y_out, d_ff_27_qn);
  and and_33 (and_33_out, Z_out, d_ff_28_qn);
  Comparator #(.width(4), .mode("unsigned")) comparator_4 (
    .a(counter_3_q), .b(4'b0000), .gt(comparator_4_gt));  // open: eq, lt
  Comparator #(.width(4), .mode("unsigned")) comparator_5 (
    .a(counter_3_q), .b(4'b0010), .gt(comparator_5_gt));  // open: eq, lt
  Comparator #(.width(4), .mode("unsigned")) comparator_6 (
    .a(counter_3_q), .b(4'b0100), .gt(comparator_6_gt));  // open: eq, lt
  Comparator #(.width(4), .mode("unsigned")) comparator_7 (
    .a(counter_3_q), .b(4'b0110), .gt(comparator_7_gt));  // open: eq, lt
  Comparator #(.width(4), .mode("unsigned")) comparator_8 (
    .a(counter_3_q), .b(4'b1000), .gt(comparator_8_gt));  // open: eq, lt
  LED led_1 (.in(comparator_4_gt));
  LED led_2 (.in(comparator_9_gt));
  Comparator #(.width(4), .mode("unsigned")) comparator_9 (
    .a(counter_3_q), .b(4'b0001), .gt(comparator_9_gt));  // open: eq, lt
  LED led_3 (.in(comparator_5_gt));
  Comparator #(.width(4), .mode("unsigned")) comparator_10 (
    .a(counter_3_q), .b(4'b0011), .gt(comparator_10_gt));  // open: eq, lt
  LED led_4 (.in(comparator_10_gt));
  LED led_5 (.in(comparator_6_gt));
  LED led_6 (.in(comparator_11_gt));
  Comparator #(.width(4), .mode("unsigned")) comparator_11 (
    .a(counter_3_q), .b(4'b0101), .gt(comparator_11_gt));  // open: eq, lt
  LED led_7 (.in(comparator_7_gt));
  Comparator #(.width(4), .mode("unsigned")) comparator_12 (
    .a(counter_3_q), .b(4'b0111), .gt(comparator_12_gt));  // open: eq, lt
  LED led_8 (.in(comparator_12_gt));
  LED led_9 (.in(comparator_8_gt));
  LED led_10 (.in(comparator_13_gt));
  Comparator #(.width(4), .mode("unsigned")) comparator_13 (
    .a(counter_3_q), .b(4'b1001), .gt(comparator_13_gt));  // open: eq, lt
  not not_4 (not_4_out, comparator_14_eq);
  Comparator #(.width(7)) comparator_14 (.a(counter_5_q), .b(7'b0000111), .eq(comparator_14_eq));  // open: gt, lt
  Comparator #(.width(7)) comparator_15 (.a(counter_5_q), .b(7'b0000001), .gt(comparator_15_gt));  // open: eq, lt
  Comparator #(.width(7)) comparator_16 (.a(counter_5_q), .b(7'b0000001), .eq(comparator_16_eq));  // open: gt, lt
  not not_5 (not_5_out, comparator_16_eq);
  Comparator #(.width(7)) comparator_17 (.a(counter_5_q), .b(7'b0000010), .eq(comparator_17_eq));  // open: gt, lt
  not not_6 (not_6_out, comparator_17_eq);
  Comparator #(.width(7)) comparator_18 (.a(counter_5_q), .b(7'b0000011), .eq(comparator_18_eq));  // open: gt, lt
  not not_7 (not_7_out, comparator_18_eq);
  not not_8 (not_8_out, comparator_19_eq);
  Comparator #(.width(7)) comparator_19 (.a(counter_5_q), .b(7'b0000111), .eq(comparator_19_eq));  // open: gt, lt
  Comparator #(.width(7)) comparator_20 (.a(counter_5_q), .b({7{1'b0}}), .eq(comparator_20_eq));  // open: gt, lt
  Comparator #(.width(7)) comparator_21 (.a(counter_5_q), .b(7'b0000010), .eq(comparator_21_eq));  // open: gt, lt
  Comparator #(.width(7)) comparator_22 (.a(counter_5_q), .b(7'b0000110), .eq(comparator_22_eq));  // open: gt, lt
  Comparator #(.width(7)) comparator_23 (.a(counter_5_q), .b(7'b0001000), .eq(comparator_23_eq));  // open: gt, lt
  and and_34 (and_34_out, not_4_out, comparator_15_gt);
  and and_35 (and_35_out, not_5_out, not_6_out, not_7_out, not_8_out);
  _7_Segment_Display u_7_segment_display_1 (
    .g(and_34_out), .f(and_35_out), .a(and_36_out), .b(and_37_out), .e(or_2_out), .d(and_38_out),
    .c(not_16_out));  // open: dp
  or or_2 (or_2_out, comparator_20_eq, comparator_21_eq, comparator_22_eq, comparator_23_eq);
  Comparator #(.width(7)) comparator_24 (.a(counter_5_q), .b(7'b0000001), .eq(comparator_24_eq));  // open: gt, lt
  Comparator #(.width(7)) comparator_25 (.a(counter_5_q), .b(7'b0000100), .eq(comparator_25_eq));  // open: gt, lt
  Comparator #(.width(7)) comparator_26 (.a(counter_5_q), .b(7'b0000101), .eq(comparator_26_eq));  // open: gt, lt
  Comparator #(.width(7)) comparator_27 (.a(counter_5_q), .b(7'b0000110), .eq(comparator_27_eq));  // open: gt, lt
  Comparator #(.width(7)) comparator_28 (.a(counter_5_q), .b(7'b0000001), .eq(comparator_28_eq));  // open: gt, lt
  Comparator #(.width(7)) comparator_29 (.a(counter_5_q), .b(7'b0000100), .eq(comparator_29_eq));  // open: gt, lt
  Comparator #(.width(7)) comparator_30 (.a(counter_5_q), .b(7'b0000111), .eq(comparator_30_eq));  // open: gt, lt
  Comparator #(.width(7)) comparator_31 (.a(counter_5_q), .b(7'b0000010), .eq(comparator_31_eq));  // open: gt, lt
  not not_9 (not_9_out, comparator_24_eq);
  and and_36 (and_36_out, not_9_out, not_10_out);
  not not_10 (not_10_out, comparator_25_eq);
  not not_11 (not_11_out, comparator_26_eq);
  and and_37 (and_37_out, not_11_out, not_12_out);
  not not_12 (not_12_out, comparator_27_eq);
  not not_13 (not_13_out, comparator_28_eq);
  not not_14 (not_14_out, comparator_29_eq);
  and and_38 (and_38_out, not_13_out, not_14_out, not_15_out);
  not not_15 (not_15_out, comparator_30_eq);
  not not_16 (not_16_out, comparator_31_eq);

  // Notes on the sheet:
  //   h
  //   e
  //   l
  //   l
  //   o
endmodule

module _7_segment (
);

  wire and_1_out, and_2_out, and_3_out, and_4_out, and_5_out, clock_1_out, comparator_1_eq, comparator_2_gt,
       comparator_3_eq, comparator_4_eq, comparator_5_eq, comparator_6_eq, comparator_7_eq, comparator_8_eq,
       comparator_9_eq, comparator_10_eq, comparator_11_eq, comparator_12_eq, comparator_13_eq,
       comparator_14_eq, comparator_15_eq, comparator_16_eq, comparator_17_eq, comparator_18_eq, not_1_out,
       not_2_out, not_3_out, not_4_out, not_5_out, not_6_out, not_7_out, not_8_out, not_9_out, not_10_out,
       not_11_out, not_12_out, not_13_out, or_1_out;
  wire [6:0] counter_1_q;

  Counter #(.width(7), .max('h9)) counter_1 (.Q(counter_1_q), .clk(clock_1_out));  // open: load, D, count, carry, clr
  Clock clock_1 (.out(clock_1_out));
  not not_1 (not_1_out, comparator_1_eq);
  Comparator #(.width(7)) comparator_1 (.a(counter_1_q), .b(7'b0000111), .eq(comparator_1_eq));  // open: gt, lt
  Comparator #(.width(7)) comparator_2 (.a(counter_1_q), .b(7'b0000001), .gt(comparator_2_gt));  // open: eq, lt
  not not_2 (not_2_out, comparator_3_eq);
  Comparator #(.width(7)) comparator_3 (.a(counter_1_q), .b(7'b0000001), .eq(comparator_3_eq));  // open: gt, lt
  not not_3 (not_3_out, comparator_4_eq);
  Comparator #(.width(7)) comparator_4 (.a(counter_1_q), .b(7'b0000010), .eq(comparator_4_eq));  // open: gt, lt
  Comparator #(.width(7)) comparator_5 (.a(counter_1_q), .b(7'b0000011), .eq(comparator_5_eq));  // open: gt, lt
  not not_4 (not_4_out, comparator_5_eq);
  not not_5 (not_5_out, comparator_6_eq);
  Comparator #(.width(7)) comparator_6 (.a(counter_1_q), .b(7'b0000111), .eq(comparator_6_eq));  // open: gt, lt
  Comparator #(.width(7)) comparator_7 (.a(counter_1_q), .b({7{1'b0}}), .eq(comparator_7_eq));  // open: gt, lt
  Comparator #(.width(7)) comparator_8 (.a(counter_1_q), .b(7'b0000010), .eq(comparator_8_eq));  // open: gt, lt
  Comparator #(.width(7)) comparator_9 (.a(counter_1_q), .b(7'b0000110), .eq(comparator_9_eq));  // open: gt, lt
  Comparator #(.width(7)) comparator_10 (.a(counter_1_q), .b(7'b0001000), .eq(comparator_10_eq));  // open: gt, lt
  and and_1 (and_1_out, not_1_out, comparator_2_gt);
  and and_2 (and_2_out, not_2_out, not_3_out, not_4_out, not_5_out);
  _7_Segment_Display u_7_segment_display_1 (
    .g(and_1_out), .f(and_2_out), .a(and_3_out), .b(and_4_out), .e(or_1_out), .d(and_5_out), .c(not_13_out));  // open: dp
  or or_1 (or_1_out, comparator_7_eq, comparator_8_eq, comparator_9_eq, comparator_10_eq);
  Comparator #(.width(7)) comparator_11 (.a(counter_1_q), .b(7'b0000001), .eq(comparator_11_eq));  // open: gt, lt
  Comparator #(.width(7)) comparator_12 (.a(counter_1_q), .b(7'b0000100), .eq(comparator_12_eq));  // open: gt, lt
  Comparator #(.width(7)) comparator_13 (.a(counter_1_q), .b(7'b0000101), .eq(comparator_13_eq));  // open: gt, lt
  Comparator #(.width(7)) comparator_14 (.a(counter_1_q), .b(7'b0000110), .eq(comparator_14_eq));  // open: gt, lt
  Comparator #(.width(7)) comparator_15 (.a(counter_1_q), .b(7'b0000001), .eq(comparator_15_eq));  // open: gt, lt
  Comparator #(.width(7)) comparator_16 (.a(counter_1_q), .b(7'b0000100), .eq(comparator_16_eq));  // open: gt, lt
  Comparator #(.width(7)) comparator_17 (.a(counter_1_q), .b(7'b0000111), .eq(comparator_17_eq));  // open: gt, lt
  Comparator #(.width(7)) comparator_18 (.a(counter_1_q), .b(7'b0000010), .eq(comparator_18_eq));  // open: gt, lt
  not not_6 (not_6_out, comparator_11_eq);
  and and_3 (and_3_out, not_6_out, not_7_out);
  not not_7 (not_7_out, comparator_12_eq);
  not not_8 (not_8_out, comparator_13_eq);
  and and_4 (and_4_out, not_8_out, not_9_out);
  not not_9 (not_9_out, comparator_14_eq);
  not not_10 (not_10_out, comparator_15_eq);
  not not_11 (not_11_out, comparator_16_eq);
  not not_12 (not_12_out, comparator_17_eq);
  not not_13 (not_13_out, comparator_18_eq);
  and and_5 (and_5_out, not_10_out, not_11_out, not_12_out);
endmodule
